# Fritzing sketch DHT_WiFi2 (saved by Fritzing 0.9.2b)
circuit board: 9.14278cm x 6.19378cm
breadboards: 1

parts:
  Часть1 = Arduino Uno (Rev3)
  LCD1 = LCD screen
  R1 = PHOTOCELL [package=photocell-kit]
  RHT1 = Humidity and Temperature Sensor RHT03
  R2 = Resistor [tolerance=±5% resistance=10 package="0805 [SMD]"]
  U2 = POT [package=pot_mammoth]
  S2 = Toggle Switch [package=THT]
  U3 = ESP8266 WiFi Module [part_number=ESP8266]  # not connected
  U4 = ESP8266 WiFi Module [part_number=ESP8266]

nets:
  N1: Часть1.A0, R1.P$1, R2.Pin_1
  N2: Часть1.D8, U4.TXD
  N3: Часть1.D9_PWM, U4.RXD
  N4: Часть1.D10_PWM/SS, LCD1.E
  N5: Часть1.D11_PWM/MOSI, LCD1.R/W
  N6: Часть1.D12/MISO, LCD1.RS
  GND: Часть1.GND, LCD1.VSS, LCD1.LED-, RHT1.GND_2, R2.Pin_0, U2.S, U4.GND
  N7: Часть1.D2, LCD1.DB7
  N8: Часть1.D3_PWM, LCD1.DB6
  N9: Часть1.D4, LCD1.DB5
  N10: Часть1.D5_PWM, LCD1.DB4
  N11: Часть1.D7, RHT1.Data-signal
  3V3: Часть1.3V3, U4.VCC, U4.CH_PD
  5V: Часть1.5V, LCD1.VDD, R1.P$2, RHT1.Vcc, U2.E, S2.COM
  N12: LCD1.V0, U2.A
  N13: LCD1.LED+, S2.L1

custom parts:
  ESP8266 WiFi Module: Generic WiFi Module based on the ESP8266 with onboard PCB antenna and UART communications

// code stored in the sketch: dht_wifi.ino
#include "DHT.h"													 // include DHT lib for humidity and temperature sensor
#include "LiquidCrystal.h"								 // include LCD lib for 1602 LCD diplay	
#include "SoftwareSerial.h"								 // include	Software Serial lib for ESP8266 

#define DHTPIN 7                           // DHT11 pin
#define DHTTYPE DHT11                      // DHT 11 

LiquidCrystal lcd(12, 11, 10, 5, 4, 3, 2); //lcd pins
SoftwareSerial esp8266(8, 9);              //esp pins

int photocellPin = 0;                      // the cell and 10K pulldown are connected to a0
int photocellReading;                      // the analog reading from the sensor divider

int dropDataCounter = 0;

int led = 13;

DHT dht(DHTPIN, DHTTYPE);                  // init dht


//======================Setup
void setup() {
  Serial.begin(9600);                      // HW serial Arduino <> computer
  delay(1000);                             // timeout init
  esp8266.begin(9600);                     // SW serial Arduino <> ESP8266, more speed more unstable. 9600 is quite enough
  pinMode(led, OUTPUT);
  dht.begin();                             // start humidity sensor
  lcd.begin(16, 2);                        // start lcd screen
  lcd.print(">");                          // print loading screen
  lcd.setCursor(0, 1);                     // -- 
  lcd.print("[i] start v0.1  ");           // --   
  lcd.setCursor(1, 0);                     // --
  digitalWrite(led, LOW);                  // turn off builtin arduino led

  Serial.println("humidity and temperature over wifi"); // serial debug out 
  Serial.println("----------------------------------"); // --
  Serial.println("[INFO] initialization");              // --

  esp8266.println("AT+RST");                            // reset ESP8266 module
  delay(1000);                                          // wait till ESP8266 is up
  lcd.print(">");                                       // print loading screen
  if (esp8266.find("ready")) {                          // if ESP8266 up and ready
    Serial.println("[INFO] ESP8266 is up");             // Serial debug print log
    lcd.print(">");                                     // print loading screen
    lcd.setCursor(0, 1);                                // --
    lcd.print("[i] ESP is up  ");                       // --
    lcd.setCursor(3, 0);                                // --
  }
  else                                                  // if ESP8266 is down
  {
    Serial.println("[ERROR] ESP8266 no response.");     // Serial debug print log
    lcd.setCursor(0, 1);																// print loading screen
    lcd.print("[E] ESP is NA  ");												// --
    lcd.setCursor(3, 0);																// --
    while (1);																					// hang
  }
  delay(500);                                           // wait more
  lcd.print(">");																				// print loading screen

  																											// connect to the wifi
  boolean connected = false;														// satate 
  for (int i = 0; i < 5; i++)                           // try 5 times to connect
  {
    if (connectWiFi()) {																// if connected
      connected = true;                                 // set state = true
      lcd.print(">");                                   // print loading screen
      lcd.setCursor(0, 1);															// --
      lcd.print("[i] WiFi cncted ");										// --
      lcd.setCursor(4, 0);															// --
      break;																						// breaf for cycle
    }
  }
  if (!connected) {																			// if still not connected
    lcd.setCursor(0, 1);																// print loading screen
    lcd.print("[E] WiFi cnct NA");											// --
    lcd.setCursor(4, 0);																// --
    while (1);                                          // hang
  }

  delay(5000);																					// wait 5 sec
  lcd.print(">");                                       // print loading screen
  lcd.setCursor(0, 1);																	// -- 
  lcd.print("[i] Obtain IP   ");												// --			
  lcd.setCursor(5, 0);																	// --
  
  esp8266.println("AT+CIFSR");													// try to get IP value. not critical. [WIP] 
  Serial.println(esp8266.println("AT+CIFSR"));
  if (esp8266.available()) 
  {
    while (esp8266.available())
    {
      char c = esp8266.read();
      Serial.write(c);
    }
  }
  																
  esp8266.println("AT+CIPMUX=0");												// set the single connection mode
  lcd.print(">");																				// print loading screen
  lcd.setCursor(0, 1);																	// --
  lcd.print("[i] CIPMUX:0    ");												// --
  lcd.setCursor(6, 0);																	// --
  delay(1000);																					// wait a sec
  esp8266.println("AT+CIPMODE=0");											// set "not data mode" duplex mode (get/send data)
  lcd.print(">");																				// print loading screen
  lcd.setCursor(0, 1);																	// --
  lcd.print("[i] CIPMODE:0   ");												// --
  lcd.setCursor(7, 0);																	// --		
  delay(1000);																					// wait a sec	
  lcd.print(">");																				// --	
  lcd.setCursor(0, 1);																	// --
  lcd.print("[i] init sensrs ");												// fake message, sensors already init	
  lcd.setCursor(7, 0);																	// --
  delay(1000);																					// wait a sec	
  lcd.print(">");                                       // --
  delay(150);																						// --
  lcd.print(">");																				// --	
  delay(120);																						// --
  lcd.print(">");																				// --	
  delay(110);																						// --
  lcd.print(">");																				// --	
  delay(90);																						// --
  lcd.print(">");																				// --	
  delay(80);																						// --
  lcd.print(">");																				// --		
  delay(70);																						// --
  lcd.print("GO!");																			// --
  delay(500);																						// --	
}

void loop() {
  
  lcd.clear();
  photocellReading = analogRead(photocellPin);                      //read photocell data

 																																		// Reading temperature or humidity takes about 250 milliseconds!
  																																  // Sensor readings may also be up to 2 seconds 'old' (its a very slow sensor)
  int h = dht.readHumidity();																						
  int t = dht.readTemperature();																		// Read temperature as Celsius

  																																	// Check if any reads failed and exit early (to try again).
  if (isnan(h) || isnan(t)) {
    lcd.setCursor(0, 0);
    Serial.println("Failed to read from DHT sensor!");
    lcd.print("Failed to read from DHT sensor!");
    return;
  }


  lcd.setCursor(0, 0);     																					// set lcd cursor to 0,0 upper string, first element on left side
  lcd.print("T:");																									// T: for Temperature
  lcd.print(t);        																							// temp value from DHT 11
  lcd.print((char)223);																							// graduses sign
  lcd.print("C ");																									// C for Celsius
  lcd.print("H:");																									// H: for Humidity
  lcd.print(h);																											// humidity value from DHT11
  lcd.print("%");																										// percent sign

  lcd.setCursor(0, 1);     																					// set lcd cursor to 0,1 bottom string, first element on left side
  lcd.print("L:");         																					// L: for Light sensor\photo sensor
  lcd.print(photocellReading);         															// photo sensor value

  delay(100);   																										// wait 100ms
  if(dropDataCounter>100){																					// On backend server sends every 100 values. Ajust delay or if statement for more result or less
    dropDataCounter = 0;																						// Set data counter is 0
    String cmd = "AT+CIPSTART=\"TCP\",\"";													// start bulding connection to backend server
    cmd += "89.108.88.25";																					// IP address of backend server
    cmd += "\",3415";																								// backend server PORT
    esp8266.println(cmd);																						// send connection command to ESP8266 
    Serial.println(cmd);																						// serial debug out 
    if (esp8266.find("Error")) {																		// error connection
      return;																												// return;
    }																																	
    cmd = "POST /?t=";																							// building POST request
    cmd += t;																												// --
    cmd += "&h=";																										// --
    cmd += h;																												// --
    cmd += "&l=";																										// --		
    cmd += photocellReading;																				// --			
    cmd += " HTTP/1.0\r\nHost: test.iot.domain\r\nConnection: close\r\nUUID: a9ad2cd7-9973-4c6a-a7a4-16002dc481f7\r\n\r\n";
    esp8266.print("AT+CIPSEND=");																		// send sending command to ESP8266
    esp8266.println(cmd.length());																	// calculate length of the POST request
    if (esp8266.find(">"))																					// send mode success
    {
      //Serial.print(">");
    } else																													// send mode error
    {
      esp8266.println("AT+CIPCLOSE");																// close connection
      Serial.println("[WARN] Connect timeout");											// serial debug out 
      delay(15000);																									// wait 15 sec
      return;																												// return
    }
    esp8266.print(cmd);																							// finaly send data to backend server	
    Serial.print(cmd);																							// serial debug out 
    delay(2000);																										// wait 2 sec			

    while (esp8266.available())																			// read answer
    {
      char c = esp8266.read();																			// --
    }
  }
  delay(500);																												// wait 500 ms
  dropDataCounter++;																								// increase data counter
}

boolean connectWiFi()																								// wifi connection function
{																																		
  esp8266.println("AT+CWMODE=1");																		// set ESP8266 to STA mode: 1 = WiFi client, 2 = Soft AP (router), 3 = both.
  String cmd = "AT+CWJAP=\"";																				// build connection string
  cmd += "ngr-g";																										// wifi network SSID, hidden supported
  cmd += "\",\"";																										// --
  cmd += "GUgu34rNok";																							// wifi password
  cmd += "\"";																											// --
  Serial.println("[INFO] Connecting to ngr-g");											// serial debug out 
  esp8266.println(cmd);																							// send connection commant to ESP8266
  delay(2000);																											// connection established in 1-5 secs
  if (esp8266.find("OK"))																						// if connection success
  {
    Serial.println("[INFO] Connected to WiFi.");										// serial debug out 
    return true;																										// return true
  } else
  {
    Serial.println("[ERROR] Can not connect to the WiFi.");					// serial debug out 
    return false;																										// return false
  }
}
